// Logisim project ULA+Teclado.circ as structural Verilog: 1 circuit, main circuit main
// zera
module main (
  input  in_1,
  input  in_2,
  input  in_3,
  input  in_4,
  input  in_5,
  input  in_6,
  input  in_7,
  input  in_8,
  output [6:0] out_9,
  output [3:0] out_10,
  output [6:0] out_11,
  output [3:0] out_12,
  output out_13
);

  wire a1, and_2_out, and_3_out, and_4_out, and_5_out, and_6_out, \botão_1 , clock_1_out, clock_2_out,
       clock_3_out, comparator_1_eq, comparator_2_eq, comparator_3_eq, comparator_4_eq, comparator_5_eq,
       comparator_6_eq, comparator_7_gt, comparator_7_lt, contador_ram, counter_4_carry, counter_5_carry,
       load, not_1_out, not_2_out, not_3_out, not_4_out, or_1_out, or_3_out, or_5_out, or_6_out,
       parar_comparador, register_1_q, verifica_oi, zera, zera_meu_nome_e, zera_oi;
  wire [2:0] counter_2_q, teste;
  wire [3:0] counter_1_q, counter_3_q, counter_4_q, counter_5_q;
  wire [4:0] counter_7_q;
  wire [6:0] buffer_1_out, meu_nome_e, multiplexer_1_out, multiplexer_2_out, oi, \output , ram_oi,
       rom_1_data, rom_3_data, rom_4_data, saidaRam2;

  Keyboard keyboard_1 (.clk(\botão_1 ), .re(in_6), .clr(in_4), .avail(a1), .data(out_11));
  Clock clock_1 (.out(clock_1_out));
  or or_1 (or_1_out, not_1_out, zera);
  not not_1 (not_1_out, in_6);
  Comparator #(.width(7)) comparator_1 (.a(out_11), .b(7'b0001010), .eq(comparator_1_eq));  // open: gt, lt
  Comparator #(.width(7)) comparator_2 (.a(\output ), .b(7'b0001010), .eq(comparator_2_eq));  // open: gt, lt
  and and_1 (\botão_1 , in_6, clock_1_out);
  Counter #(.width(4), .max('hf)) counter_1 (
    .load(in_8), .Q(counter_1_q), .clk(\botão_1 ), .clr(or_1_out));  // open: D, count, carry
  Multiplexer #(.width(7), .enable("false")) multiplexer_1 (
    .in0(out_11), .in1(oi), .out(multiplexer_1_out), .sel(verifica_oi));
  assign buffer_1_out = out_11;  // Buffer buffer_1, 7 bits wide
  not not_2 (not_2_out, in_6);
  not not_3 (not_3_out, in_6);
  D_Flip_Flop d_ff_1 (.clk(comparator_1_eq), .D(comparator_1_eq), .Q(load), .reset(zera));  // open: Qn, preset, en
  and and_2 (and_2_out, comparator_2_eq, verifica_oi);
  Multiplexer #(.width(7), .enable("false")) multiplexer_2 (
    .in0(multiplexer_1_out), .in1(meu_nome_e), .out(multiplexer_2_out), .sel(parar_comparador));
  TTY tty_1 (.data(multiplexer_2_out), .clk(\botão_1 ), .we(\botão_1 ), .clr(in_3));
  not not_4 (not_4_out, parar_comparador);
  or or_2 (contador_ram, not_2_out, zera);
  Counter #(.width(3), .max('h3)) counter_2 (
    .load(in_5), .Q(counter_2_q), .clk(\botão_1 ), .clr(or_3_out));  // open: D, count, carry
  or or_3 (or_3_out, not_3_out, zera);
  ROM #(.addrWidth(4), .dataWidth(7)) rom_1 (.addr(counter_1_q), .data(rom_1_data));  // open: sel
  D_Flip_Flop d_ff_2 (.clk(and_2_out), .D(and_2_out), .Q(out_13), .reset(zera));  // open: Qn, preset, en
  Counter #(.width(4), .max('hf)) counter_3 (
    .count(not_4_out), .Q(counter_3_q), .clk(\botão_1 ), .clr(contador_ram));  // open: load, D, carry
  Comparator #(.width(7)) comparator_3 (.a(rom_1_data), .b(saidaRam2), .eq(comparator_3_eq));  // open: gt, lt
  Counter #(.width(4), .max('hf), .ongoal("stay")) counter_4 (
    .Q(counter_4_q), .carry(counter_4_carry), .clk(comparator_3_eq), .clr(zera));  // open: load, D, count
  RAM #(.addrWidth(4), .dataWidth(7), .bus("separate")) ram_1 (
    .addr(counter_3_q), .din(buffer_1_out), .data(out_9), .str(a1), .clk(\botão_1 ), .ld(load),
    .clr(contador_ram));  // open: sel
  ROM #(.addrWidth(3), .dataWidth(7)) rom_2 (.addr(counter_2_q), .data(ram_oi));  // open: sel
  Counter #(.width(4), .max('hf), .ongoal("stay")) counter_5 (
    .Q(counter_5_q), .carry(counter_5_carry), .clk(comparator_4_eq), .clr(zera));  // open: load, D, count
  Comparator #(.width(7)) comparator_4 (.a(saidaRam2), .b(ram_oi), .eq(comparator_4_eq));  // open: gt, lt
  or or_4 (zera, in_7, zera_oi);
  Comparator #(.width(7)) comparator_5 (.a(out_9), .b(7'b0001010), .eq(comparator_5_eq));  // open: gt, lt
  Multiplexer #(.width(4), .enable("false")) multiplexer_3 (
    .in0(4'b0000), .in1(counter_5_q), .out(out_12), .sel(counter_5_carry));
  Comparator #(.width(7)) comparator_6 (.a(oi), .b({7{1'b0}}), .eq(comparator_6_eq));  // open: gt, lt
  Multiplexer #(.width(4), .enable("false")) multiplexer_4 (
    .in0(4'b0000), .in1(counter_4_q), .out(out_10), .sel(counter_4_carry));
  Register #(.width(1)) register_1 (
    .D(comparator_5_eq), .Q(register_1_q), .clk(comparator_5_eq), .clr(zera));  // open: en
  Comparator #(.width(4)) comparator_7 (
    .a(out_10), .b(out_12), .gt(comparator_7_gt), .lt(comparator_7_lt));  // open: eq
  Clock clock_2 (.out(clock_2_out));
  Clock clock_3 (.out(clock_3_out));
  Multiplexer #(.width(7), .enable("false")) multiplexer_5 (
    .in1(out_9), .out(saidaRam2), .sel(register_1_q));  // open: in0
  and and_3 (and_3_out, comparator_6_eq, or_5_out);
  or or_5 (or_5_out, zera_oi, zera_meu_nome_e);
  and and_4 (and_4_out, verifica_oi, clock_2_out);
  and and_5 (and_5_out, parar_comparador, clock_3_out);
  Comparator #(.width(1)) comparator_8 (.a(in_1), .b(in_2));  // open: gt, eq, lt
  Register #(.width(1)) register_2 (
    .D(comparator_7_gt), .Q(verifica_oi), .clk(comparator_7_gt), .clr(or_6_out));  // open: en
  and and_6 (and_6_out, verifica_oi, and_3_out);
  Counter #(.width(3), .max('h4), .ongoal("stay")) counter_6 (
    .Q(teste), .clk(and_4_out), .clr(zera));  // open: load, D, count, carry
  Counter #(.width(5), .max('h10), .ongoal("stay")) counter_7 (
    .Q(counter_7_q), .clk(and_5_out), .clr(zera));  // open: load, D, count, carry
  or or_6 (or_6_out, zera, and_6_out);
  Register #(.width(1)) register_3 (
    .D(comparator_7_lt), .Q(parar_comparador), .clk(comparator_7_lt), .clr(zera));  // open: en
  Comparator #(.width(7)) comparator_9 (.a({7{1'b0}}), .b(rom_3_data), .eq(zera_oi));  // open: gt, lt
  ROM #(.addrWidth(3), .dataWidth(7)) rom_3 (.addr(teste), .data(rom_3_data));  // open: sel
  Comparator #(.width(7)) comparator_10 (.a({7{1'b0}}), .b(rom_4_data), .eq(zera_meu_nome_e));  // open: gt, lt
  ROM #(.addrWidth(5), .dataWidth(7)) rom_4 (.addr(counter_7_q), .data(rom_4_data));  // open: sel
  Multiplexer #(.width(7), .enable("false")) multiplexer_6 (.in0(rom_3_data), .out(oi), .sel(zera_oi));  // open: in1
  Multiplexer #(.width(7), .enable("false")) multiplexer_7 (
    .in0(rom_4_data), .in1({7{1'b0}}), .out(meu_nome_e), .sel(zera_meu_nome_e));

  // Other names for the same wires on the sheet: input[6:0] = out_11; Ligar = in_6; Nome[3:0] = out_10;
  //   saida_RAM[6:0] = out_9; verifica_meu_nome_e = parar_comparador; zera_o_clock_oi = verifica_oi

  // Notes on the sheet:
  //   contents of rom_1 (hex, n*v repeats v):
  //   71 75 61 6c 20 6f 20 73 65 75 20 6e 6f 6d 65 a
  //   contents of rom_2 (hex, n*v repeats v):
  //   6f 69 a
  //   Zera os clocks
  //   Respostas do bot
  //   Respostas do bot
  //   contents of rom_3 (hex, n*v repeats v):
  //   11 6f 69 a
  //   contents of rom_4 (hex, n*v repeats v):
  //   11 6d 65 75 20 6e 6f 6d 65 20 65 20 61 6e 61 a
endmodule
